# Fritzing sketch home-automation-model (saved by Fritzing 0.9.3b)
breadboards: 1

parts:
  U1 = NodeMCU V1.0
  U2 = 2-Channel 5v Relay Shield [package=relay-2ch5v10a]
  LED1 = smd LED [color="Red (633nm)" package="0805 [SMD]"]
  R1 = Resistor [tolerance=±5% resistance=220 package="0603 [SMD]"]

nets:
  N1: U1.D0, U2.IN1
  N2: U1.D1, U2.K1-In
  GND: U1.GND, U2.GND, R1.Pin_0
  VIN: U1.Vin, U2.VCC
  N3: U2.K1-On, LED1.anode
  N4: LED1.cathode, R1.Pin_1

notes:
  Power supply for the ESP8266 might as well occur through:
  - A USB port
  - A supply regulator connected to a battery
  - A phone charger
  - A 9v battery
  ESP8266 has a tension regulator of 3.3v
  Is connected to power via a USB cable

custom parts:
  NodeMCU V1.0: ESP8266 based NodeMCU
  2-Channel 5v Relay Shield: 2 Channel 5v Relay Shield w. 2x SPD-06VDC-SD-C
